# Fritzing sketch HUB Module (saved by Fritzing 1.0.2b)
circuit board: 3.6289cm x 2.68036cm
breadboards: 1

parts:
  FE1_1S = SSOP28DB [chip_label=SSOP28DB package=SSOP]
  12MHz = OSCILLATOR [package=crystal-smd-3.2x2.5]
  VDD_D-_D+_GND = female pin header, 4 pins [form="♀ (female)"]
  VDD_D-_D+_GND_2 = female pin header, 4 pins [form="♀ (female)"]
  GND_D+_D-_VDD = female pin header, 4 pins [form="♀ (female)"]
  VDD_D-_D+_GND_3 = female pin header, 4 pins [form="♀ (female)"]
  330µF = Capacitor Polarized [package=cpol-radial-100uf-25v]
  330µF_2 = Capacitor Polarized [package=cpol-radial-100uf-25v]
  2_7KΩ = Resistor [tolerance=±5% resistance=220 package="0805 [SMD]"]
  10µF = Ceramic Capacitor [capacitance=10µF voltage=35V package="0805 [SMD, multilayer]"]
  10µF_2 = Ceramic Capacitor [capacitance=10µF voltage=35V package="0805 [SMD, multilayer]"]
  100KΩ = Resistor [tolerance=±5% resistance=220 package="0805 [SMD]"]
  100KΩ_2 = Resistor [tolerance=±5% resistance=220 package="0805 [SMD]"]
  100KΩ_3 = Resistor [tolerance=±5% resistance=220 package="0805 [SMD]"]
  VDD_D-_D+_GND_4 = female pin header, 4 pins [form="♀ (female)"]
  100KΩ_4 = Resistor [tolerance=±5% resistance=220 package="0805 [SMD]"]
  47KΩ = Resistor [tolerance=±5% resistance=220 package="0805 [SMD]"]
  100nF = Ceramic Capacitor [capacitance=10µF voltage=35V package="0805 [SMD, multilayer]"]
  4_7µF = Ceramic Capacitor [capacitance=10µF voltage=35V package="0805 [SMD, multilayer]"]
  +5V_GND = female pin header, 2 pins [form="♀ (female)"]
  10uF = Ceramic Capacitor [capacitance=10µF voltage=35V package="0805 [SMD, multilayer]"]

nets:
  N1: FE1_1S.1, 12MHz.GND#1, VDD_D-_D+_GND_3.pin1, 330µF.-, 10µF.0, 10µF_2.0, 100KΩ_3.Pin_1, +5V_GND.pin2, 10uF.1
  N2: FE1_1S.2, 12MHz.Pad2
  N3: FE1_1S.3, 12MHz.Pad_1
  N4: FE1_1S.4, VDD_D-_D+_GND_3.pin3
  N5: FE1_1S.5, VDD_D-_D+_GND_3.pin2
  N6: FE1_1S.6, VDD_D-_D+_GND.pin3
  N7: FE1_1S.7, VDD_D-_D+_GND.pin2
  N8: FE1_1S.8, VDD_D-_D+_GND_2.pin3
  N9: FE1_1S.9, VDD_D-_D+_GND_2.pin2
  N10: FE1_1S.10, GND_D+_D-_VDD.pin3
  N11: FE1_1S.11, GND_D+_D-_VDD.pin2
  N12: FE1_1S.12, FE1_1S.28, 10µF.1
  N13: FE1_1S.13, FE1_1S.21, FE1_1S.26, 10µF_2.1, 100KΩ.Pin_1, 100KΩ_2.Pin_1
  N14: FE1_1S.14, 2_7KΩ.Pin_1
  N15: FE1_1S.15, VDD_D-_D+_GND_4.pin3
  N16: FE1_1S.16, VDD_D-_D+_GND_4.pin2
  N17: FE1_1S.17, 100KΩ_2.Pin_0
  N18: FE1_1S.18, 100KΩ_4.Pin_0, 47KΩ.Pin_0
  N19: FE1_1S.19, 100KΩ.Pin_0
  N20: FE1_1S.20, VDD_D-_D+_GND_4.pin4, 47KΩ.Pin_1, 100nF.1, 4_7µF.1
  N21: FE1_1S.22, 100KΩ_3.Pin_0
  N22: 12MHz.GND#3, VDD_D-_D+_GND.pin1, VDD_D-_D+_GND_2.pin1, GND_D+_D-_VDD.pin1, 330µF_2.-, 2_7KΩ.Pin_0, VDD_D-_D+_GND_4.pin1, 100KΩ_4.Pin_1, 100nF.0, 4_7µF.0
  N23: VDD_D-_D+_GND.pin4, VDD_D-_D+_GND_2.pin4, GND_D+_D-_VDD.pin4, VDD_D-_D+_GND_3.pin4, 330µF.+, 330µF_2.+, +5V_GND.pin1, 10uF.0
