# Fritzing sketch TTL Module (saved by Fritzing 1.0.2b)
circuit board: 2.06569cm x 1.24953cm
breadboards: 1

parts:
  CP2102 = Single-Chip USB to UART Bridge [package=mlp28]
  VDD_D-_D+_GND = female pin header, 4 pins [form="♀ (female)"]
  100nF = Ceramic Capacitor [capacitance="100 nF" voltage=35V package="0805 [SMD, multilayer]"]
  100nF_2 = Ceramic Capacitor [capacitance="100 nF" voltage=35V package="0805 [SMD, multilayer]"]
  RX_TX_GND = female pin header, 3 pins [form="♀ (female)"]

nets:
  N1: CP2102.GND, VDD_D-_D+_GND.pin1, 100nF.0, 100nF_2.0, RX_TX_GND.pin1
  N2: CP2102.D+, VDD_D-_D+_GND.pin2
  N3: CP2102.D-, VDD_D-_D+_GND.pin3
  N4: CP2102.VDD, 100nF.1
  N5: CP2102.REGIN, CP2102.VBUS, VDD_D-_D+_GND.pin4, 100nF_2.1
  N6: CP2102.RXD, RX_TX_GND.pin3
  N7: CP2102.TXD, RX_TX_GND.pin2
